// Logisim project sagui.circ as structural Verilog: 6 circuits, main circuit main
module main (
);

  wire clk, comparator_1_eq;
  wire [7:0] adder_2_out, bankreg_1_out_6, bankreg_1_out_7, memControl_data, memInst_data, multiplexer_1_out,
       multiplexer_2_out, multiplexer_3_out, multiplexer_5_out, pcImm, ram_1_dout, register_1_q, ula_1_s;

  Register register_1 (.D(multiplexer_1_out), .clk(clk), .Q(register_1_q));  // open: en, clr
  Multiplexer #(.select(2), .width(8)) multiplexer_1 (
    .in0(adder_2_out), .in1(bankreg_1_out_7), .in2(multiplexer_3_out), .in3(pcImm), .out(multiplexer_1_out));  // open: sel
  Clock clock_1 (.out(clk));
  ROM memInst (.addr(register_1_q), .data(memInst_data));
  Adder adder_1 (.a(register_1_q), .out(pcImm));  // open: b, cin, cout
  Adder adder_2 (.a(8'h1), .b(register_1_q), .out(adder_2_out));  // open: cin, cout
  Multiplexer #(.width(8)) multiplexer_2 (
    .in0(bankreg_1_out_7), .in1(multiplexer_5_out), .out(multiplexer_2_out));  // open: sel
  ROM #(.addrWidth(4)) memControl (.addr(memInst_data[7:4]), .data(memControl_data));
  bankReg bankreg_1 (
    .WB(multiplexer_2_out), .ra(memInst_data[1:0]), .rb(memInst_data[3:2]), .clk(clk),
    .out_6(bankreg_1_out_6), .out_7(bankreg_1_out_7));  // open: WE
  Multiplexer #(.width(8)) multiplexer_3 (
    .in0(adder_2_out), .in1(bankreg_1_out_7), .out(multiplexer_3_out), .sel(comparator_1_eq));
  Comparator comparator_1 (.a(bankreg_1_out_6), .b({8{1'b0}}), .eq(comparator_1_eq));  // open: gt, lt
  Multiplexer #(.width(8)) multiplexer_4 (.in0(adder_2_out), .in1(pcImm));  // open: out, sel
  ula ula_1 (.a(bankreg_1_out_6), .b(bankreg_1_out_7), .s(ula_1_s));  // open: sel, Imm, CntrHL
  RAM ram_1 (.addr(bankreg_1_out_7), .clk(clk), .din(bankreg_1_out_6), .dout(ram_1_dout));  // open: we, oe
  Multiplexer #(.width(8)) multiplexer_5 (.in0(ula_1_s), .in1(ram_1_dout), .out(multiplexer_5_out));  // open: sel

  // Notes on the sheet:
  //   JUMP (PC + iMM)
  //   Jump Register
  //   opcode
  //   Branch On Zero Register
endmodule

module bankReg (
  input  [7:0] WB,
  input  WE,
  input  [1:0] ra,
  input  [1:0] rb,
  input  clk,
  output [7:0] out_6,
  output [7:0] out_7
);

  wire reg1, reg2, reg3, reg4;
  wire [7:0] register_1_q, register_2_q, register_3_q, register_4_q;

  Demultiplexer #(.select(2)) demultiplexer_1 (.out0(reg1), .out1(reg2), .out2(reg3), .out3(reg4), .in(WE), .sel(ra));
  Register register_1 (.D(WB), .en(reg1), .clk(clk), .Q(register_1_q));  // open: clr
  Register register_2 (.D(WB), .en(reg2), .clk(clk), .Q(register_2_q));  // open: clr
  Register register_3 (.D(WB), .en(reg3), .clk(clk), .Q(register_3_q));  // open: clr
  Register register_4 (.D(WB), .en(reg4), .clk(clk), .Q(register_4_q));  // open: clr
  Multiplexer #(.select(2), .width(8)) multiplexer_1 (
    .in0(register_1_q), .in1(register_2_q), .in2(register_3_q), .in3(register_4_q), .out(out_6), .sel(ra));
  Multiplexer #(.select(2), .width(8)) multiplexer_2 (
    .in0(register_1_q), .in1(register_2_q), .in2(register_3_q), .in3(register_4_q), .out(out_7), .sel(rb));
endmodule

module ula (
  input  [7:0] a,
  input  [7:0] b,
  input  [2:0] sel,
  input  [3:0] Imm,
  input  CntrHL,
  output [7:0] s
);

  wire [7:0] adder_1_out, and_1_out, deslocdir_1_s, deslocesq_1_s, move_1_s, not_1_out, or_1_out,
       subtractor_1_out;

  Adder adder_1 (.a(a), .b(b), .out(adder_1_out));  // open: cin, cout
  Subtractor subtractor_1 (.a(a), .b(b), .out(subtractor_1_out));  // open: bin, bout
  assign and_1_out = a & b;  // AND_Gate and_1, 8 bits wide
  assign or_1_out = a | b;  // OR_Gate or_1, 8 bits wide
  assign not_1_out = ~b;  // NOT_Gate not_1, 8 bits wide
  deslocDir deslocdir_1 (.regA(a), .regB(b), .s(deslocdir_1_s));
  deslocEsq deslocesq_1 (.regA(a), .regB(b), .s(deslocesq_1_s));
  move move_1 (.regA(a), .imm(Imm), .ctrl(CntrHL), .s(move_1_s));
  Multiplexer #(.select(3), .width(8)) multiplexer_1 (
    .in0(adder_1_out), .in1(subtractor_1_out), .in2(and_1_out), .in3(or_1_out), .in4(not_1_out),
    .in5(deslocdir_1_s), .in6(deslocesq_1_s), .in7(move_1_s), .out(s), .sel(sel));
endmodule

module deslocDir (
  input  [7:0] regA,
  input  [7:0] regB,
  output [7:0] s
);

  wire or_1_out;
  wire [7:0] shifter_1_out;

  or or_1 (or_1_out, regB[3], regB[4], regB[5], regB[6], regB[7]);
  Shifter #(.shift("lr")) shifter_1 (.in(regA), .\dist (regB[2:0]), .out(shifter_1_out));
  Multiplexer #(.width(8)) multiplexer_1 (.in0(shifter_1_out), .in1({8{1'b0}}), .out(s), .sel(or_1_out));
endmodule

module deslocEsq (
  input  [7:0] regA,
  input  [7:0] regB,
  output [7:0] s
);

  wire or_1_out;
  wire [7:0] shifter_1_out;

  or or_1 (or_1_out, regB[3], regB[4], regB[5], regB[6], regB[7]);
  Shifter shifter_1 (.in(regA), .\dist (regB[2:0]), .out(shifter_1_out));
  Multiplexer #(.width(8)) multiplexer_1 (.in0(shifter_1_out), .in1({8{1'b0}}), .out(s), .sel(or_1_out));
endmodule

module move (
  input  [7:0] regA,
  input  [3:0] imm,
  input  ctrl,
  output [7:0] s
);
endmodule
